# Fritzing sketch WaveShareSchaltpläne (saved by Fritzing 1.0.1rc)

parts:
  RobotBoard_1_2_H3/H4 = Camdenboss CTB0158-6 [part_number=CTB0158-6 package=THT]
  TT_Motor_Encoder = Camdenboss CTB0158-6 [part_number=CTB0158-6 package=THT]

nets:
  N1: RobotBoard_1_2_H3/H4.pin1, TT_Motor_Encoder.pin6
  N2: RobotBoard_1_2_H3/H4.pin2, TT_Motor_Encoder.pin1
  N3: RobotBoard_1_2_H3/H4.pin3, TT_Motor_Encoder.pin3
  N4: RobotBoard_1_2_H3/H4.pin4, TT_Motor_Encoder.pin2
  N5: RobotBoard_1_2_H3/H4.pin5, TT_Motor_Encoder.pin4
  N6: RobotBoard_1_2_H3/H4.pin6, TT_Motor_Encoder.pin5
