# Fritzing sketch Untitled Sketch (saved by Fritzing 1.0.1rc)

parts:
  U1 = ESP32-38PinWide [part_number=ESP32-38PinWide]
  Bauteil1 = Thumb Joystick
  R1 = Rotary Potentiometer (Large) [maximum_resistance=100kΩ knob_status=50% power=0.5W package=THT]
  R2 = Rotary Potentiometer (Large) [maximum_resistance=100kΩ knob_status=50% power=0.5W package=THT]

nets:
  N1: U1.3.3, R2.leg1
  N2: U1.GPIO25, R2.wiper
  N3: U1.GPIO26, R1.wiper
  N4: U1.GPIO27, Bauteil1.VERT
  N5: U1.GPIO14, Bauteil1.HORZ
  N6: U1.GPIO12, Bauteil1.SEL
  N7: U1.GPIO11, R2.leg2

custom parts:
  ESP32-38PinWide: Generic 38-Pin ESP32 with wide format (only access to one side of pins on a breadboard) based on Stephen Lilley's HiLetgo ESP-WROOM-32 ESP32 ESP-32S Development Board.
