# Fritzing sketch Esp32Neo6M (saved by Fritzing 0.9.4)

parts:
  U1 = ESP32-38PinWide [part_number=ESP32-38PinWide]
  Bauteil1 = u-blox NEO-6M GPS Breakout

nets:
  N1: U1.3.3, Bauteil1.VCC
  N2: U1.GPIO4, Bauteil1.TXD
  N3: U1.GPIO16, Bauteil1.RXD
  GND: U1.GND, Bauteil1.GND

custom parts:
  ESP32-38PinWide: Generic 38-Pin ESP32 with wide format (only access to one side of pins on a breadboard) based on Stephen Lilley's HiLetgo ESP-WROOM-32 ESP32 ESP-32S Development Board.
